# Fritzing sketch P3 (saved by Fritzing 0.9.3b)
breadboards: 1

parts:
  R10 = Resistor [tolerance=±5% resistance=220 package=THT]
  IR = TSOP312.., 314.. [package=THT]
  J1 = Piezo Speaker
  R11 = Resistor [tolerance=±5% resistance=220 package=THT]
  Part1 = RFID-RC522-v3
  LED1 = RGB LED (com. cathode, rgb) [package="5 mm [THT]"]
  R9 = Resistor [tolerance=±5% resistance=220 package=THT]
  U1 = NodeMCU V1.0

nets:
  N1: R10.Pin_0, LED1.red_anode
  N2: R10.Pin_1, U1.D2
  GND: IR.GND, J1.pin1, Part1.GND, LED1.common_cathode, U1.GND
  3.3V: IR.Vs, Part1.3.3V, U1.3V3
  N3: IR.Data, U1.D1
  N4: J1.pin2, U1.D0
  N5: R11.Pin_0, LED1.blue_anode
  N6: R11.Pin_1, U1.D4
  N7: Part1.SDA, U1.D8
  N8: Part1.SCK, U1.D5
  N9: Part1.MOSI, U1.D7
  N10: Part1.MISO, U1.D6
  N11: LED1.green_anode, R9.Pin_0
  N12: R9.Pin_1, U1.D3

custom parts:
  RFID-RC522-v3: A simple China made RFID-RC522 Reader (6x4 cm); do check the pin labels, as this is a MFRC522 based clone.
  NodeMCU V1.0: ESP8266 based NodeMCU
